# Fritzing sketch Protoboard (saved by Fritzing 0.7.12b)
breadboards: 1

parts:
  Arduino2 = Arduino
  LED1 = LED - 5mm [color="Red (633nm)" package="5 mm [THT]"]
  LED2 = LED - 5mm [color="Red (633nm)" package="5 mm [THT]"]
  LED3 = LED - 5mm [color="Red (633nm)" package="5 mm [THT]"]
  LED4 = LED - 5mm [color="Red (633nm)" package="5 mm [THT]"]
  LED5 = LED - 5mm [color="Red (633nm)" package="5 mm [THT]"]
  LED6 = LED - 5mm [color="Red (633nm)" package="5 mm [THT]"]
  LED7 = LED - 5mm [color="Red (633nm)" package="5 mm [THT]"]
  LED8 = LED - 5mm [color="Red (633nm)" package="5 mm [THT]"]
  LED9 = LED - 5mm [color="Red (633nm)" package="5 mm [THT]"]
  LED10 = LED - 5mm [color="Red (633nm)" package="5 mm [THT]"]
  LED11 = LED - 5mm [color="Red (633nm)" package="5 mm [THT]"]
  R1 = Resistor [tolerance=±5% resistance=220 package=THT]
  R2 = Resistor [tolerance=±5% resistance=220 package=THT]
  R3 = Resistor [tolerance=±5% resistance=220 package=THT]
  R4 = Resistor [tolerance=±5% resistance=220 package=THT]
  R5 = Resistor [tolerance=±5% resistance=220 package=THT]
  R6 = Resistor [tolerance=±5% resistance=220 package=THT]
  R7 = Resistor [tolerance=±5% resistance=220 package=THT]
  R8 = Resistor [tolerance=±5% resistance=220 package=THT]
  R9 = Resistor [tolerance=±5% resistance=220 package=THT]
  R10 = Resistor [tolerance=±5% resistance=220 package=THT]
  R11 = Resistor [tolerance=±5% resistance=220 package=THT]
  S1 = Pushbutton [package="[THT]"]
  S2 = Pushbutton [package="[THT]"]
  R12 = Resistor [tolerance=±5% resistance=2.2k package=THT]
  R13 = Resistor [tolerance=±5% resistance=220 package=THT]

nets:
  N1: Arduino2.GND, LED1.anode, LED2.anode, LED3.anode, LED4.anode, LED5.anode, LED6.anode, LED7.anode, LED8.anode, LED9.anode, LED10.anode, LED11.anode, S1.Pin_3, S1.Pin_4, S2.Pin_3, S2.Pin_4
  N2: Arduino2.D13, R10.Pin_0
  N3: Arduino2.D12, R2.Pin_0
  N4: Arduino2.D11, R4.Pin_0
  N5: Arduino2.D10, R3.Pin_0
  N6: Arduino2.D9, R5.Pin_0
  N7: Arduino2.D8, R1.Pin_0
  N8: Arduino2.D2, S1.Pin_1, S1.Pin_2, R12.Pin_0
  N9: Arduino2.+5V, R12.Pin_1, R13.Pin_1
  N10: Arduino2.A0, R6.Pin_0
  N11: Arduino2.A1, R7.Pin_0
  N12: Arduino2.A2, R8.Pin_0
  N13: Arduino2.A3, R9.Pin_0
  N14: Arduino2.A4, R11.Pin_0
  N15: LED1.cathode, R1.Pin_1
  N16: LED2.cathode, R5.Pin_1
  N17: LED3.cathode, R3.Pin_1
  N18: LED4.cathode, R4.Pin_1
  N19: LED5.cathode, R2.Pin_1
  N20: LED6.cathode, R10.Pin_1
  N21: LED7.cathode, R6.Pin_1
  N22: LED8.cathode, R7.Pin_1
  N23: LED9.cathode, R8.Pin_1
  N24: LED10.cathode, R9.Pin_1
  N25: LED11.cathode, R11.Pin_1
  N26: S2.Pin_1, S2.Pin_2, R13.Pin_0
